# Fritzing sketch shield (saved by Fritzing 0.9.9b)
circuit board: 6.5cm x 3.2cm
breadboards: 1

parts:
  U1 = SUP500F [package=sup500f]
  J4 = female pin header, 4 pins [form="♀ (female)"]
  S1 = Round Pushbutton
  J5 = Piezo Speaker
  J2 = Raspberry Pi Header 40pin [form="♂ (male)" package=THT]

nets:
  N1: U1.RX-I, J4.pin2, J2.GIPO15
  N2: U1.TX-O, J4.pin3, J2.GIPO14
  GND: U1.GND, J4.pin1, S1.leg0, J5.pin1, J2.GND
  VCC: U1.VCC, J4.pin4, J2.5V
  N3: S1.leg1, J2.GPIO3
  N4: J5.pin2, J2.GIPO21

notes:
  yellow - RX
  blue - TX
  black - GND
  red - VCC
  RX
  TX
  GND
  VCC
  PWR_BTN
  piezo
  github.com/
  jsfraz/trek-tracker

custom parts:
  Raspberry Pi Header 40pin: Raspberry Pi 40 pin header - for creating your own shields.
